# Fritzing sketch schematic (saved by Fritzing 0.9.3b)

parts:
  Part1 = Arduino Mega 2560 (Rev3)
  J4 = Basic Servo
  J5 = Basic Servo
  J6 = Basic Servo
  J7 = Basic Servo
  J8 = Basic Servo
  J9 = Basic Servo
  U1 = LM2596 step down module
  VCC1 = Battery block 9V
  U2 = LM2596 step down module
  GLCD_128x1 = 128 x 64 Graphic LCD  # not connected
  Raspberry_Pi_1 = Raspberry Pi 3 [part_number=RPI-3-V1.2]
  U3 = TRANSCHIPTC5747 [package=camera_sfv24r-2st_2]  # not connected

nets:
  N1: Part1.D13_PWM, J5.pulse
  N2: Part1.D12_PWM, J6.pulse
  N3: Part1.D11_PWM, J4.pulse
  N4: Part1.D10_PWM, J7.pulse
  N5: Part1.D9_PWM, J8.pulse
  N6: Part1.D8_PWM, J9.pulse
  GND: Part1.GND, J9.gnd
  VIN: Part1.VIN, J9.vcc
  N7: U1.IN+, VCC1.+, U2.IN+
  N8: VCC1.-, U2.IN-, U2.OUT-, Raspberry_Pi_1.GIPO20
  N9: U2.OUT+, Raspberry_Pi_1.GIPO21

notes:
  FUENTE DE PODER 24V

custom parts:
  LM2596 step down module: LM2596 DC-DC step down power supply module 3 A.
